# Fritzing sketch featherwing-proto (saved by Fritzing 0.9.3b)

parts:
  FeatherWing_Proto = Adafruit FeatherWing Proto [part_number="Adafruit #2884"]
  RGBLED = RGB LED - (4 legs) [package="5 mm [THT]"]
  R_R = Resistor [tolerance=±5% resistance=220 package=THT]
  R_G = Resistor [tolerance=±5% resistance=220 package=THT]
  R_B = Resistor [tolerance=±5% resistance=220 package=THT]

nets:
  N1: FeatherWing_Proto.N, R_R.Pin_0
  N2: FeatherWing_Proto.M, R_G.Pin_0
  N3: FeatherWing_Proto.L, R_B.Pin_0
  N4: FeatherWing_Proto.3V, FeatherWing_Proto.N$121, FeatherWing_Proto.N$132, RGBLED.common_anode
  N5: FeatherWing_Proto.N$119, FeatherWing_Proto.N$130, RGBLED.blue_cathode, R_B.Pin_1
  N6: FeatherWing_Proto.N$120, FeatherWing_Proto.N$131, RGBLED.green_cathode, R_G.Pin_1
  N7: FeatherWing_Proto.N$122, FeatherWing_Proto.N$133, RGBLED.red_cathode, R_R.Pin_1

custom parts:
  Adafruit FeatherWing Proto: This is the FeatherWing Proto - a prototyping add-on for all Feather boards. Using our Feather Stacking Headers or Feather Female Headers you can connect a FeatherWing on top or bottom of your Feather board and let the board take flight! This has a duplicate breakout for each pin on a Feather, as well as a bunch of plain grid proto holes. For GND and 3.3V, we give you a strip of connected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
